# Fritzing sketch BaseDisplay_Keypad_Buzzer (saved by Fritzing 0.9.4)
breadboards: 1

parts:
  Part1 = Arduino Nano (Rev3.0)
  R1 = Resistor [tolerance=±5% resistance=1k package=THT]
  Q1 = NPN-Transistor [part_number=2N2222 package="TO92 [THT]"]
  Q2 = NPN-Transistor [part_number=2N2222 package="TO92 [THT]"]
  R2 = Resistor [tolerance=±5% resistance=1k package=THT]
  R3 = Resistor [tolerance=±5% resistance=1k package=THT]
  R4 = Resistor [tolerance=±5% resistance=1k package=THT]
  R5 = Resistor [tolerance=±5% resistance=1k package=THT]
  Q3 = NPN-Transistor [part_number=2N2222 package="TO92 [THT]"]
  Q5 = NPN-Transistor [part_number=2N2222 package="TO92 [THT]"]
  R6 = Resistor [tolerance=±5% resistance=330 package=THT]
  R7 = Resistor [tolerance=±5% resistance=330 package=THT]
  R8 = Resistor [tolerance=±5% resistance=330 package=THT]
  R9 = Resistor [tolerance=±5% resistance=330 package=THT]
  R10 = Resistor [tolerance=±5% resistance=330 package=THT]
  R11 = Resistor [tolerance=±5% resistance=330 package=THT]
  R12 = Resistor [tolerance=±5% resistance=330 package=THT]
  Q4 = NPN-Transistor [package="TO92 [THT]"]
  MX4-301C1 = MX4-301C [package="DIP (Dual Inline) [THT]"]
  Componente1 = 4x4 Keypad [part_number=101207]
  R13 = Resistor [tolerance=±5% resistance=10k package=THT]
  R14 = Resistor [tolerance=±5% resistance=10k package=THT]
  R15 = Resistor [tolerance=±5% resistance=10k package=THT]
  IC1 = IC, DIP package, 14 pins [chip_label="CD 4066"]
  R16 = Resistor [tolerance=±5% resistance=10k package=THT]
  R17 = Resistor [tolerance=±5% resistance=10k package=THT]
  R18 = Resistor [tolerance=±5% resistance=10k package=THT]
  R19 = Resistor [tolerance=±5% resistance=10k package=THT]
  J1 = Piezo Speaker

nets:
  N1: Part1.GND, Q1.E, Q2.E, Q3.E, Q5.E, Q4.E, IC1.pin7, R16.Pin_1, R17.Pin_1, R18.Pin_0, R19.Pin_0, J1.pin1
  N2: Part1.D2, R7.Pin_1
  N3: Part1.D3, R6.Pin_1
  N4: Part1.D4, R12.Pin_1
  N5: Part1.D5, R11.Pin_1
  N6: Part1.D6, R10.Pin_1
  N7: Part1.D7, J1.pin2
  N8: Part1.D8, R9.Pin_1
  N9: Part1.D9, R8.Pin_1
  N10: Part1.D11/MOSI, R4.Pin_1
  N11: Part1.D12/MISO, R5.Pin_1, IC1.pin13
  N12: Part1.VIN, IC1.pin2, IC1.pin3, IC1.pin9, IC1.pin10
  N13: Part1.5V, Componente1.1, R13.Pin_0, IC1.pin14
  N14: Part1.A3, R1.Pin_0, IC1.pin6
  N15: Part1.A2, R2.Pin_0, IC1.pin5
  N16: Part1.A1, R3.Pin_0, IC1.pin12
  N17: R1.Pin_1, Q1.B
  N18: Q1.C, MX4-301C1.pin10
  N19: Q2.B, R2.Pin_1
  N20: Q2.C, MX4-301C1.pin8
  N21: R3.Pin_1, Q3.B
  N22: R4.Pin_0, Q4.B
  N23: R5.Pin_0, Q5.B
  N24: Q3.C, MX4-301C1.pin5
  N25: Q5.C, MX4-301C1.pin2
  N26: R6.Pin_0, MX4-301C1.pin3, MX4-301C1.pin7
  N27: R7.Pin_0, MX4-301C1.pin1, MX4-301C1.pin20
  N28: R8.Pin_0, MX4-301C1.pin4, MX4-301C1.pin19
  N29: R9.Pin_0, MX4-301C1.pin17, MX4-301C1.pin23
  N30: R10.Pin_0, MX4-301C1.pin12, MX4-301C1.pin22
  N31: R11.Pin_0, MX4-301C1.pin15, MX4-301C1.pin18
  N32: R12.Pin_0, MX4-301C1.pin9, MX4-301C1.pin11, MX4-301C1.pin21
  N33: Q4.C, MX4-301C1.pin6, MX4-301C1.pin13, MX4-301C1.pin14, MX4-301C1.pin16, MX4-301C1.pin24
  N34: Componente1.2, R13.Pin_1, R14.Pin_0
  N35: Componente1.3, R14.Pin_1, R15.Pin_1
  N36: Componente1.4, R15.Pin_0
  N37: Componente1.5, IC1.pin1, R16.Pin_0
  N38: Componente1.6, IC1.pin4, R17.Pin_0
  N39: Componente1.7, IC1.pin8, R18.Pin_1
  N40: Componente1.8, IC1.pin11, R19.Pin_1

custom parts:
  MX4-301C: Four digits 7 segments LED display - common cathode
  4x4 Keypad: Matrix membrane keypad 4x4
